// Logisim project 2_input_mux.circ as structural Verilog: 1 circuit, main circuit mux2
module mux2 (
  input  input0,
  input  input1,
  input  select,
  output \output 
);

  wire and_1_out, and_2_out, not_1_out;

  not not_1 (not_1_out, select);
  and and_1 (and_1_out, input0, not_1_out);
  and and_2 (and_2_out, select, input1);
  or or_1 (\output , and_1_out, and_2_out);
endmodule
