// Logisim project 4_adder.circ as structural Verilog: 1 circuit, main circuit adders
module adders (
  input  a0,
  input  b0,
  input  carry_in,
  input  a1,
  input  b1,
  input  a2,
  input  b2,
  input  a3,
  input  b3,
  output result0,
  output out_11,
  output result1,
  output out_13,
  output result2,
  output out_15,
  output result3,
  output out_17,
  output carry_out,
  output out_19
);

  wire and_1_out, and_3_out, and_5_out, and_7_out, and_9_out, and_11_out, and_13_out, and_15_out, and_17_out,
       and_19_out, and_21_out, and_23_out, and_25_out, and_27_out, and_29_out, and_31_out, and_33_out,
       and_35_out, and_37_out, and_39_out, not_1_out, not_3_out, not_5_out, not_7_out, not_9_out, not_11_out,
       not_13_out, not_15_out, or_1_out, or_3_out, or_5_out, or_7_out, or_9_out, or_11_out, or_13_out,
       or_15_out, or_17_out, or_19_out, or_21_out;

  and and_1 (and_1_out, a0, b0);
  and and_2 (and_1_out, a0, b0);
  or or_1 (or_1_out, a0, b0);
  or or_2 (or_1_out, a0, b0);
  and and_3 (and_3_out, b0, a0);
  and and_4 (and_3_out, b0, a0);
  and and_5 (and_5_out, a1, b1);
  and and_6 (and_5_out, a1, b1);
  or or_3 (or_3_out, a1, b1);
  or or_4 (or_3_out, a1, b1);
  and and_7 (and_7_out, b1, a1);
  and and_8 (and_7_out, b1, a1);
  and and_9 (and_9_out, a2, b2);
  and and_10 (and_9_out, a2, b2);
  or or_5 (or_5_out, a2, b2);
  or or_6 (or_5_out, a2, b2);
  and and_11 (and_11_out, b2, a2);
  and and_12 (and_11_out, b2, a2);
  and and_13 (and_13_out, a3, b3);
  and and_14 (and_13_out, a3, b3);
  or or_7 (or_7_out, a3, b3);
  or or_8 (or_7_out, a3, b3);
  and and_15 (and_15_out, b3, a3);
  and and_16 (and_15_out, b3, a3);
  not not_1 (not_1_out, and_1_out);
  not not_2 (not_1_out, and_1_out);
  not not_3 (not_3_out, and_5_out);
  not not_4 (not_3_out, and_5_out);
  not not_5 (not_5_out, and_9_out);
  not not_6 (not_5_out, and_9_out);
  not not_7 (not_7_out, and_13_out);
  not not_8 (not_7_out, and_13_out);
  and and_17 (and_17_out, not_1_out, or_1_out);
  and and_18 (and_17_out, not_1_out, or_1_out);
  and and_19 (and_19_out, not_3_out, or_3_out);
  and and_20 (and_19_out, not_3_out, or_3_out);
  and and_21 (and_21_out, not_5_out, or_5_out);
  and and_22 (and_21_out, not_5_out, or_5_out);
  and and_23 (and_23_out, not_7_out, or_7_out);
  and and_24 (and_23_out, not_7_out, or_7_out);
  and and_25 (and_25_out, and_17_out, carry_in);
  not not_9 (not_9_out, and_25_out);
  and and_26 (and_25_out, and_17_out, carry_in);
  not not_10 (not_9_out, and_25_out);
  or or_9 (or_9_out, and_17_out, carry_in);
  or or_10 (or_9_out, and_17_out, carry_in);
  and and_27 (and_27_out, and_17_out, carry_in);
  and and_28 (and_27_out, and_17_out, carry_in);
  and and_29 (and_29_out, and_19_out, or_17_out);
  not not_11 (not_11_out, and_29_out);
  and and_30 (and_29_out, and_19_out, or_17_out);
  not not_12 (not_11_out, and_29_out);
  or or_11 (or_11_out, and_19_out, or_17_out);
  or or_12 (or_11_out, and_19_out, or_17_out);
  and and_31 (and_31_out, and_19_out, or_17_out);
  and and_32 (and_31_out, and_19_out, or_17_out);
  and and_33 (and_33_out, and_21_out, or_19_out);
  and and_34 (and_33_out, and_21_out, or_19_out);
  not not_13 (not_13_out, and_33_out);
  not not_14 (not_13_out, and_33_out);
  or or_13 (or_13_out, and_21_out, or_19_out);
  or or_14 (or_13_out, and_21_out, or_19_out);
  and and_35 (and_35_out, and_21_out, or_19_out);
  and and_36 (and_35_out, and_21_out, or_19_out);
  and and_37 (and_37_out, and_23_out, or_21_out);
  not not_15 (not_15_out, and_37_out);
  and and_38 (and_37_out, and_23_out, or_21_out);
  not not_16 (not_15_out, and_37_out);
  or or_15 (or_15_out, and_23_out, or_21_out);
  or or_16 (or_15_out, and_23_out, or_21_out);
  and and_39 (and_39_out, and_23_out, or_21_out);
  and and_40 (and_39_out, and_23_out, or_21_out);
  and and_41 (out_11, not_9_out, or_9_out);
  and and_42 (out_11, not_9_out, or_9_out);
  or or_17 (or_17_out, and_27_out, and_3_out);
  or or_18 (or_17_out, and_27_out, and_3_out);
  and and_43 (out_13, not_11_out, or_11_out);
  and and_44 (out_13, not_11_out, or_11_out);
  or or_19 (or_19_out, and_31_out, and_7_out);
  or or_20 (or_19_out, and_31_out, and_7_out);
  and and_45 (out_15, not_13_out, or_13_out);
  and and_46 (out_15, not_13_out, or_13_out);
  or or_21 (or_21_out, and_35_out, and_11_out);
  or or_22 (or_21_out, and_35_out, and_11_out);
  and and_47 (out_17, not_15_out, or_15_out);
  and and_48 (out_17, not_15_out, or_15_out);
  or or_23 (carry_out, and_39_out, and_15_out);
  or or_24 (carry_out, and_39_out, and_15_out);

  assign out_19 = carry_out;
  assign result0 = out_11;
  assign result1 = out_13;
  assign result2 = out_15;
  assign result3 = out_17;
endmodule
