// Logisim project 4_alu.circ as structural Verilog: 1 circuit, main circuit alu
module alu (
  input  a0,
  input  b0,
  input  control0,
  input  control1,
  input  carry_in,
  input  a1,
  input  b1,
  input  a2,
  input  b2,
  input  a3,
  input  b3,
  output result0,
  output result1,
  output result2,
  output result3,
  output carry_out
);

  wire and_1_out, and_2_out, and_3_out, and_4_out, and_5_out, and_6_out, and_7_out, and_8_out, and_9_out,
       and_10_out, and_11_out, and_12_out, and_13_out, and_14_out, and_15_out, and_16_out, and_17_out,
       and_18_out, and_19_out, and_21_out, and_23_out, and_24_out, and_26_out, and_28_out, and_29_out,
       and_31_out, and_33_out, and_34_out, and_35_out, and_36_out, and_38_out, and_40_out, and_42_out,
       and_43_out, and_44_out, and_46_out, and_47_out, and_48_out, and_50_out, and_51_out, and_52_out,
       and_54_out, and_56_out, and_58_out, and_60_out, and_62_out, and_64_out, and_66_out, and_68_out,
       and_70_out, and_72_out, and_74_out, and_76_out, not_1_out, not_2_out, not_3_out, not_4_out, not_5_out,
       not_6_out, not_7_out, not_8_out, not_9_out, not_10_out, not_11_out, not_13_out, not_14_out,
       not_16_out, not_17_out, not_19_out, not_20_out, not_22_out, not_24_out, not_26_out, not_28_out,
       or_1_out, or_2_out, or_3_out, or_4_out, or_5_out, or_6_out, or_7_out, or_9_out, or_10_out, or_12_out,
       or_13_out, or_15_out, or_16_out, or_18_out, or_20_out, or_22_out, or_24_out, or_26_out, or_28_out,
       or_30_out;

  not not_1 (not_1_out, control0);
  and and_1 (and_1_out, control1, b0);
  or or_1 (or_1_out, b0, control1);
  and and_2 (and_2_out, control1, b1);
  or or_2 (or_2_out, b1, control1);
  and and_3 (and_3_out, control1, b2);
  or or_3 (or_3_out, b2, control1);
  and and_4 (and_4_out, control1, b3);
  or or_4 (or_4_out, b3, control1);
  not not_2 (not_2_out, and_1_out);
  not not_3 (not_3_out, and_2_out);
  not not_4 (not_4_out, and_3_out);
  not not_5 (not_5_out, and_4_out);
  and and_5 (and_5_out, not_2_out, or_1_out);
  and and_6 (and_6_out, not_3_out, or_2_out);
  and and_7 (and_7_out, not_4_out, or_3_out);
  and and_8 (and_8_out, not_5_out, or_4_out);
  or or_5 (or_5_out, control1, carry_in);
  not not_6 (not_6_out, not_1_out);
  not not_7 (not_7_out, not_1_out);
  not not_8 (not_8_out, not_1_out);
  not not_9 (not_9_out, not_1_out);
  and and_9 (and_9_out, not_6_out, a0);
  and and_10 (and_10_out, not_6_out, and_5_out);
  and and_11 (and_11_out, not_6_out, or_5_out);
  and and_12 (and_12_out, not_7_out, a1);
  and and_13 (and_13_out, not_7_out, and_6_out);
  and and_14 (and_14_out, not_8_out, a2);
  and and_15 (and_15_out, not_8_out, and_7_out);
  and and_16 (and_16_out, not_9_out, a3);
  and and_17 (and_17_out, not_9_out, and_8_out);
  and and_18 (and_18_out, a0, and_5_out);
  not not_10 (not_10_out, control1);
  or or_6 (or_6_out, a0, and_5_out);
  and and_19 (and_19_out, and_9_out, and_10_out);
  and and_20 (and_19_out, and_9_out, and_10_out);
  or or_7 (or_7_out, and_9_out, and_10_out);
  or or_8 (or_7_out, and_9_out, and_10_out);
  and and_21 (and_21_out, and_10_out, and_9_out);
  and and_22 (and_21_out, and_10_out, and_9_out);
  and and_23 (and_23_out, a1, and_6_out);
  or or_9 (or_9_out, a1, and_6_out);
  and and_24 (and_24_out, and_12_out, and_13_out);
  and and_25 (and_24_out, and_12_out, and_13_out);
  or or_10 (or_10_out, and_12_out, and_13_out);
  or or_11 (or_10_out, and_12_out, and_13_out);
  and and_26 (and_26_out, and_13_out, and_12_out);
  and and_27 (and_26_out, and_13_out, and_12_out);
  and and_28 (and_28_out, a2, and_7_out);
  or or_12 (or_12_out, a2, and_7_out);
  and and_29 (and_29_out, and_14_out, and_15_out);
  and and_30 (and_29_out, and_14_out, and_15_out);
  or or_13 (or_13_out, and_14_out, and_15_out);
  or or_14 (or_13_out, and_14_out, and_15_out);
  and and_31 (and_31_out, and_15_out, and_14_out);
  and and_32 (and_31_out, and_15_out, and_14_out);
  and and_33 (and_33_out, a3, and_8_out);
  or or_15 (or_15_out, a3, and_8_out);
  and and_34 (and_34_out, and_18_out, not_10_out, not_1_out);
  and and_35 (and_35_out, not_1_out, control1, or_6_out);
  not not_11 (not_11_out, and_19_out);
  not not_12 (not_11_out, and_19_out);
  not not_13 (not_13_out, control1);
  not not_14 (not_14_out, and_24_out);
  not not_15 (not_14_out, and_24_out);
  not not_16 (not_16_out, control1);
  not not_17 (not_17_out, and_29_out);
  not not_18 (not_17_out, and_29_out);
  not not_19 (not_19_out, control1);
  and and_36 (and_36_out, and_16_out, and_17_out);
  and and_37 (and_36_out, and_16_out, and_17_out);
  not not_20 (not_20_out, and_36_out);
  not not_21 (not_20_out, and_36_out);
  or or_16 (or_16_out, and_16_out, and_17_out);
  or or_17 (or_16_out, and_16_out, and_17_out);
  and and_38 (and_38_out, and_17_out, and_16_out);
  and and_39 (and_38_out, and_17_out, and_16_out);
  and and_40 (and_40_out, not_11_out, or_7_out);
  and and_41 (and_40_out, not_11_out, or_7_out);
  and and_42 (and_42_out, and_23_out, not_13_out, not_1_out);
  and and_43 (and_43_out, not_1_out, control1, or_9_out);
  and and_44 (and_44_out, not_14_out, or_10_out);
  and and_45 (and_44_out, not_14_out, or_10_out);
  and and_46 (and_46_out, and_28_out, not_16_out, not_1_out);
  and and_47 (and_47_out, not_1_out, control1, or_12_out);
  and and_48 (and_48_out, not_17_out, or_13_out);
  and and_49 (and_48_out, not_17_out, or_13_out);
  and and_50 (and_50_out, and_33_out, not_19_out, not_1_out);
  and and_51 (and_51_out, not_1_out, control1, or_15_out);
  and and_52 (and_52_out, not_20_out, or_16_out);
  and and_53 (and_52_out, not_20_out, or_16_out);
  not not_22 (not_22_out, and_54_out);
  not not_23 (not_22_out, and_54_out);
  and and_54 (and_54_out, and_40_out, and_11_out);
  and and_55 (and_54_out, and_40_out, and_11_out);
  or or_18 (or_18_out, and_40_out, and_11_out);
  or or_19 (or_18_out, and_40_out, and_11_out);
  and and_56 (and_56_out, and_40_out, and_11_out);
  and and_57 (and_56_out, and_40_out, and_11_out);
  and and_58 (and_58_out, and_44_out, or_26_out);
  and and_59 (and_58_out, and_44_out, or_26_out);
  or or_20 (or_20_out, and_44_out, or_26_out);
  or or_21 (or_20_out, and_44_out, or_26_out);
  and and_60 (and_60_out, and_44_out, or_26_out);
  and and_61 (and_60_out, and_44_out, or_26_out);
  and and_62 (and_62_out, and_48_out, or_28_out);
  and and_63 (and_62_out, and_48_out, or_28_out);
  or or_22 (or_22_out, and_48_out, or_28_out);
  or or_23 (or_22_out, and_48_out, or_28_out);
  and and_64 (and_64_out, and_48_out, or_28_out);
  and and_65 (and_64_out, and_48_out, or_28_out);
  and and_66 (and_66_out, and_52_out, or_30_out);
  and and_67 (and_66_out, and_52_out, or_30_out);
  or or_24 (or_24_out, and_52_out, or_30_out);
  or or_25 (or_24_out, and_52_out, or_30_out);
  and and_68 (and_68_out, and_52_out, or_30_out);
  and and_69 (and_68_out, and_52_out, or_30_out);
  and and_70 (and_70_out, not_22_out, or_18_out);
  and and_71 (and_70_out, not_22_out, or_18_out);
  or or_26 (or_26_out, and_56_out, and_21_out);
  or or_27 (or_26_out, and_56_out, and_21_out);
  not not_24 (not_24_out, and_58_out);
  not not_25 (not_24_out, and_58_out);
  not not_26 (not_26_out, and_62_out);
  not not_27 (not_26_out, and_62_out);
  not not_28 (not_28_out, and_66_out);
  not not_29 (not_28_out, and_66_out);
  and and_72 (and_72_out, not_24_out, or_20_out);
  and and_73 (and_72_out, not_24_out, or_20_out);
  or or_28 (or_28_out, and_60_out, and_26_out);
  or or_29 (or_28_out, and_60_out, and_26_out);
  and and_74 (and_74_out, not_26_out, or_22_out);
  and and_75 (and_74_out, not_26_out, or_22_out);
  or or_30 (or_30_out, and_64_out, and_31_out);
  or or_31 (or_30_out, and_64_out, and_31_out);
  and and_76 (and_76_out, not_28_out, or_24_out);
  and and_77 (and_76_out, not_28_out, or_24_out);
  or or_32 (carry_out, and_68_out, and_38_out);
  or or_33 (carry_out, and_68_out, and_38_out);
  or or_34 (result0, and_34_out, and_35_out, and_70_out);
  or or_35 (result1, and_42_out, and_43_out, and_72_out);
  or or_36 (result2, and_46_out, and_47_out, and_74_out);
  or or_37 (result3, and_50_out, and_51_out, and_76_out);
endmodule
