// Logisim project 4_input_mux.circ as structural Verilog: 1 circuit, main circuit mux4
module mux4 (
  input  input0,
  input  select0,
  input  in_3,
  input  input1,
  input  input2,
  input  input3,
  output \output 
);

  wire and_1_out, and_2_out, and_3_out, and_4_out, not_1_out, not_2_out, not_3_out, or_1_out, or_2_out;

  not not_1 (not_1_out, in_3);
  not not_2 (not_2_out, select0);
  not not_3 (not_3_out, select0);
  and and_1 (and_1_out, input0, not_2_out, not_1_out);
  and and_2 (and_2_out, not_1_out, select0, input1);
  and and_3 (and_3_out, input2, in_3, not_3_out);
  and and_4 (and_4_out, select0, in_3, input3);
  or or_1 (or_1_out, and_1_out, and_2_out);
  or or_2 (or_2_out, and_3_out, and_4_out);
  or or_3 (\output , or_1_out, or_2_out);

  // Notes on the sheet:
  //   select1
endmodule
