// Logisim project 4_reg.circ as structural Verilog: 1 circuit, main circuit reg4
module reg4 (
  input  clock,
  input  write_enable,
  input  in_3,
  input  in_4,
  input  in_5,
  input  in_6,
  output output0,
  output output1,
  output output2,
  output output3
);

  wire and_1_out;

  and and_1 (and_1_out, clock, write_enable);
  flip_flop flip_flop_1 (.Q(output0), .Clock(and_1_out), .Data(in_3));  // open: nQ
  flip_flop flip_flop_2 (.Q(output1), .Clock(and_1_out), .Data(in_4));  // open: nQ
  flip_flop flip_flop_3 (.Q(output2), .Clock(and_1_out), .Data(in_5));  // open: nQ
  flip_flop flip_flop_4 (.Q(output3), .Clock(and_1_out), .Data(in_6));  // open: nQ
endmodule
