// Logisim project 4_register.circ as structural Verilog: 1 circuit, main circuit main
module main (
  input  Write_enable,
  input  data0,
  input  data1,
  input  data2,
  input  data3,
  input  Write_data,
  output output0,
  output output1,
  output output2,
  output output3
);

  wire and_1_out, and_2_out, and_3_out, and_4_out, and_5_out, and_6_out, and_7_out, and_8_out, and_9_out,
       and_10_out, and_11_out, and_12_out, and_13_out, and_14_out, and_15_out, and_16_out, and_17_out,
       and_18_out, and_19_out, and_20_out, not_1_out, not_2_out, not_3_out, not_4_out, not_5_out, not_6_out,
       not_7_out, not_8_out, not_9_out, not_10_out, not_11_out, not_12_out, not_13_out, not_14_out,
       not_15_out, not_16_out, not_17_out, not_18_out, not_19_out, not_20_out, not_22_out, not_24_out,
       not_26_out, not_28_out, or_1_out, or_2_out, or_3_out, or_4_out, or_5_out, or_6_out, or_7_out,
       or_8_out, or_9_out, or_10_out, or_11_out, or_12_out, or_13_out, or_14_out, or_15_out, or_16_out;

  and and_1 (and_1_out, Write_enable, data0);
  and and_2 (and_2_out, Write_enable, data1);
  and and_3 (and_3_out, Write_enable, data2);
  and and_4 (and_4_out, Write_enable, data3);
  not not_1 (not_1_out, Write_data);
  not not_2 (not_2_out, Write_data);
  not not_3 (not_3_out, Write_data);
  not not_4 (not_4_out, Write_data);
  and and_5 (and_5_out, and_1_out, not_1_out);
  buf and_6 (and_6_out, and_1_out);  // AND_Gate
  and and_7 (and_7_out, and_2_out, not_2_out);
  and and_8 (and_8_out, and_2_out, Write_data);
  and and_9 (and_9_out, and_3_out, not_3_out);
  and and_10 (and_10_out, and_3_out, Write_data);
  and and_11 (and_11_out, and_4_out, not_4_out);
  and and_12 (and_12_out, and_4_out, Write_data);
  or or_1 (or_1_out, and_5_out, not_7_out);
  or or_2 (or_2_out, not_6_out, and_6_out);
  or or_3 (or_3_out, and_7_out, not_10_out);
  or or_4 (or_4_out, not_9_out, and_8_out);
  or or_5 (or_5_out, and_9_out, not_13_out);
  or or_6 (or_6_out, not_12_out, and_10_out);
  or or_7 (or_7_out, and_11_out, not_16_out);
  or or_8 (or_8_out, not_15_out, and_12_out);
  not not_5 (not_5_out, and_1_out);
  not not_6 (not_6_out, or_1_out);
  not not_7 (not_7_out, or_2_out);
  not not_8 (not_8_out, and_2_out);
  not not_9 (not_9_out, or_3_out);
  not not_10 (not_10_out, or_4_out);
  not not_11 (not_11_out, and_3_out);
  not not_12 (not_12_out, or_5_out);
  not not_13 (not_13_out, or_6_out);
  not not_14 (not_14_out, and_4_out);
  not not_15 (not_15_out, or_7_out);
  not not_16 (not_16_out, or_8_out);
  not not_17 (not_17_out, not_6_out);
  not not_18 (not_18_out, not_9_out);
  not not_19 (not_19_out, not_12_out);
  not not_20 (not_20_out, not_15_out);
  and and_13 (and_13_out, not_5_out, not_17_out);
  and and_14 (and_14_out, not_5_out, not_6_out);
  and and_15 (and_15_out, not_8_out, not_18_out);
  and and_16 (and_16_out, not_8_out, not_9_out);
  and and_17 (and_17_out, not_11_out, not_19_out);
  and and_18 (and_18_out, not_11_out, not_12_out);
  and and_19 (and_19_out, not_14_out, not_20_out);
  and and_20 (and_20_out, not_14_out, not_15_out);
  or or_9 (or_9_out, and_13_out, not_22_out);
  or or_10 (or_10_out, output0, and_14_out);
  or or_11 (or_11_out, and_15_out, not_24_out);
  or or_12 (or_12_out, output1, and_16_out);
  or or_13 (or_13_out, and_17_out, not_26_out);
  or or_14 (or_14_out, output2, and_18_out);
  or or_15 (or_15_out, and_19_out, not_28_out);
  or or_16 (or_16_out, output3, and_20_out);
  not not_21 (output0, or_9_out);
  not not_22 (not_22_out, or_10_out);
  not not_23 (output1, or_11_out);
  not not_24 (not_24_out, or_12_out);
  not not_25 (output2, or_13_out);
  not not_26 (not_26_out, or_14_out);
  not not_27 (output3, or_15_out);
  not not_28 (not_28_out, or_16_out);

  // Notes on the sheet:
  //   Clock
  //   Clock
  //   Clock
  //   Clock
  //   R
  //   S
  //   R
  //   S
  //   R
  //   S
  //   R
  //   S
  //   S
  //   S
  //   S
  //   S
  //   R
  //   R
  //   R
  //   R
endmodule
