// Logisim project D_flip_flop.circ as structural Verilog: 1 circuit, main circuit flip_flop
module flip_flop (
  input  Clock,
  input  Data,
  output Q,
  output nQ
);

  wire and_1_out, and_2_out, and_3_out, and_4_out, not_1_out, not_2_out, not_3_out, not_4_out, not_5_out,
       or_1_out, or_2_out, or_3_out, or_4_out;

  and and_1 (and_1_out, Clock, not_1_out);
  not not_1 (not_1_out, Data);
  and and_2 (and_2_out, Clock, Data);
  not not_2 (not_2_out, Clock);
  not not_3 (not_3_out, or_1_out);
  or or_1 (or_1_out, and_1_out, not_4_out);
  not not_4 (not_4_out, or_2_out);
  or or_2 (or_2_out, not_3_out, and_2_out);
  not not_5 (not_5_out, not_3_out);
  and and_3 (and_3_out, not_2_out, not_5_out);
  and and_4 (and_4_out, not_2_out, not_3_out);
  or or_3 (or_3_out, and_3_out, nQ);
  or or_4 (or_4_out, Q, and_4_out);
  not not_6 (Q, or_3_out);
  not not_7 (nQ, or_4_out);

  // Notes on the sheet:
  //   R
  //   S
  //   R
  //   S
endmodule
