// Logisim project circuit.circ as structural Verilog: 1 circuit, main circuit main
module main (
  input  in_1,
  input  in_2,
  input  in_3,
  input  in_4,
  input  in_5,
  input  in_6,
  input  in_7,
  input  in_8,
  input  in_9,
  input  in_10,
  input  carry_in,
  input  in_12,
  input  in_13,
  input  in_14,
  output output0,
  output output1,
  output out_17,
  output output2,
  output output3
);

  wire reg4_1_output0, reg4_1_output1, reg4_1_output2, reg4_1_output3, reg4_2_output0, reg4_2_output1,
       reg4_2_output2, reg4_2_output3, reg4_3_p3, reg4_3_p4, reg4_3_p5, reg4_3_p6;

  reg4 reg4_1 (
    .clock(in_2), .write_enable(in_1), .in_3(in_3), .in_4(in_4), .in_5(in_5), .in_6(in_6),
    .output0(reg4_1_output0), .output1(reg4_1_output1), .output2(reg4_1_output2), .output3(reg4_1_output3));
  reg4 reg4_2 (
    .clock(in_2), .write_enable(in_1), .in_3(in_7), .in_4(in_8), .in_5(in_9), .in_6(in_10),
    .output0(reg4_2_output0), .output1(reg4_2_output1), .output2(reg4_2_output2), .output3(reg4_2_output3));
  // reg4 reg4_3: pin names not known; wires that end beside it: in_2, in_1, reg4_3_p3, reg4_3_p4, reg4_3_p5, reg4_3_p6, output0, output1, output2, output3
  alu alu_1 (
    .control0(reg4_1_output0), .control1(reg4_1_output3), .a0(reg4_1_output1), .b0(reg4_1_output2),
    .a1(reg4_2_output2), .b1(reg4_2_output3), .a2(carry_in), .b2(in_12), .a3(in_13), .b3(in_14),
    .carry_out(reg4_3_p3), .result0(reg4_3_p4), .result1(reg4_3_p5), .result2(reg4_3_p6), .result3(out_17),
    .carry_in(reg4_2_output0));

  // Notes on the sheet:
  //   clock
  //   write enable
endmodule
